# Fritzing sketch WateringMachine_ESP8266 (saved by Fritzing 0.9.3b)
breadboards: 2

parts:
  Part2 = Adafruit ADS1115 16Bit I2C ADC [part_number="Adafruit #1085"]
  NodeMCU_v2 = NodeMCU v3 LoLin [part_number=ESP8266]
  Part3 = KY-019 5V Relay Module [package="Breakout board"]
  M2 = DC Motor
  Part4 = KY-019 5V Relay Module [package="Breakout board"]  # not connected
  Power_plug2 = Power plug
  LED2 = LEDs [package=led10mm]
  Part5 = VERTER 5V USB Buck-Boost
  Part6 = Soil Moisture Sensor
  Part7 = Soil Moisture Sensor
  LED3 = LEDs [package=led10mm]
  Part8 = VERTER 5V USB Buck-Boost

nets:
  N1: Part2.AIN2, Part2.AIN1, Part7.SIG
  N2: Part2.AIN0, Part6.SIG
  GND: Part2.GND, Part6.GND, Part7.GND
  VCC: Part2.VDD, Part6.VCC, Part7.VCC
  N3: NodeMCU_v2.GND#6, NodeMCU_v2.GND#13, NodeMCU_v2.GND#16, NodeMCU_v2.GND#33, Power_plug2.GND
  VIN: NodeMCU_v2.VIN, Power_plug2.VCC
  N4: Part3.NO, M2.pin_2
  N5: LED2.A, Part5.GND
  N6: LED2.C, Part5.5.0V
  N7: LED3.A, Part8.GND
  N8: LED3.C, Part8.5.0V

custom parts:
  Adafruit ADS1115 16Bit I2C ADC: For microcontrollers without an analog-to-digital converter or when you want a higher-precision ADC, the ADS1115 provides 16-bit precision at 860 samples/second over I2C. The chip can be configured as 4 single-ended input channels, or two differential channels. As a nice bonus, it even includes a programmable gain amplifier, up to x16, to help boost up smaller single/differential signals to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
  NodeMCU v3 LoLin: NodeMCU v3 LoLin NodeMCU (http://www.nodemcu.com/) is an open source IoT platform. It includes firmware (https://nodemcu-build.com/) which runs on the ESP8266 Wi-Fi SoC from Espressif Systems, and hardware which is based on the ESP-12E module. The term "NodeMCU" by default refers to the firmware rather than the dev kits. The firmware uses the Lua scripting language. It is based on the eLua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
  KY-019 5V Relay Module: KY-019 5V Relay module, used to control AC circuits.
  LEDs: LEDs Standard schematic elements and footprints for 5mm, 3mm, 1206, and 0603 sized LEDs. 5mm - Spark Fun Electronics SKU : COM-00529 (and others)
  VERTER 5V USB Buck-Boost: VERTER can take battery voltages from 3-12VDC and output a nice 5V DC, which makes it a perfect universal power supply for your portable project! Where Verter really shines is when you have a battery or power range that can fluctuate a lot, or you don't know what you'll end up using.
